// Logisim project lfsr.circ as structural Verilog: 1 circuit, main circuit main
module main (
  input  [31:0] seed,
  input  rst
);

  wire clk_out, or_1_out, shift_register_1_q0, shift_register_1_q10, shift_register_1_q30,
       shift_register_1_q31, xor_1_out;

  Clock clk (.out(clk_out));
  Shift_Register #(.length(32)) shift_register_1 (
    .in(xor_1_out), .clk(or_1_out), .load(rst), .d0(seed[31]), .q0(shift_register_1_q0), .d1(seed[30]),
    .d2(seed[29]), .d3(seed[28]), .d4(seed[27]), .d5(seed[26]), .d6(seed[25]), .d7(seed[24]), .d8(seed[23]),
    .d9(seed[22]), .d10(seed[21]), .q10(shift_register_1_q10), .d11(seed[20]), .d12(seed[19]),
    .d13(seed[18]), .d14(seed[17]), .d15(seed[16]), .d16(seed[15]), .d17(seed[14]), .d18(seed[13]),
    .d19(seed[12]), .d20(seed[11]), .d21(seed[10]), .d22(seed[9]), .d23(seed[8]), .d24(seed[7]),
    .d25(seed[6]), .d26(seed[5]), .d27(seed[4]), .d28(seed[3]), .d29(seed[2]), .d30(seed[1]),
    .q30(shift_register_1_q30), .d31(seed[0]), .q31(shift_register_1_q31));  // open: shift, out, clr, q1, q2, q3, q4, q5, q6, q7, q8, q9, q11, q12, q13, q14, q15, q16, q17, q18, q19, q20, q21, q22, q23, q24, q25, q26, q27, q28, q29
  or or_1 (or_1_out, clk_out, rst);
  ExactlyOne xor_1 (
    .out(xor_1_out), .in0(shift_register_1_q31), .in1(shift_register_1_q30), .in2(shift_register_1_q10),
    .in3(shift_register_1_q0));
endmodule
